// Logisim project tp2.circ as structural Verilog: 2 circuits, main circuit main
module main (
  input  CLK,
  input  [3:0] Rm,
  input  [3:0] Rn,
  input  [3:0] Rd,
  input  SigEcr,
  input  [31:0] Imm,
  input  Reg_Imm,
  input  [1:0] Op
);

  wire [31:0] alu_1_sortie, banc_reg_1_valreg0, banc_reg_1_valreg1, multiplexer_1_out;

  banc_reg banc_reg_1 (
    .clk(CLK), .ValEcriture(alu_1_sortie), .IndReg0(Rm), .IndReg1(Rn), .IndRegEcr(Rd), .SigEcr(SigEcr),
    .ValReg0(banc_reg_1_valreg0), .Valreg1(banc_reg_1_valreg1));  // open: R15_in
  // Probe on banc_reg_1_valreg0
  Multiplexer #(.width(32)) multiplexer_1 (.in0(banc_reg_1_valreg1), .in1(Imm), .out(multiplexer_1_out), .sel(Reg_Imm));
  ALU alu_1 (.Op1(banc_reg_1_valreg0), .Op2(multiplexer_1_out), .Sel(Op), .Sortie(alu_1_sortie));  // open: NZCV
endmodule

module decodeur (
  input  CLK,
  input  [3:0] RS1,
  input  [3:0] RS2,
  input  [3:0] Rd,
  input  [31:0] Imm,
  input  [1:0] Rot,
  input  SigEcr,
  input  Reg_Imm
);
endmodule
